// Logisim project clock_sim.circ as structural Verilog: 1 circuit, main circuit main
module main (
  input  [7:0] stuff
);

  wire clock_1_out, n7421_1_pin1;

  Clock clock_1 (.out(clock_1_out));
  _7421 u_7421_1 (
    .pin1(n7421_1_pin1), .pin2(clock_1_out));  // open: pin3, pin4, pin5, pin6, pin13, pin12, pin11, pin10, pin9, pin8
  // Probe on n7421_1_pin1
  Counter counter_1 (.clr(n7421_1_pin1), .D(stuff));  // open: load, up, count, clk, carry, Q
endmodule
